# Fritzing sketch ActivationModule-R2 (saved by Fritzing 0.9.1b)
circuit board: 5.99934cm x 8cm
breadboards: 1

parts:
  U1 = atmega328 [package=dip]
  R1 = Resistor [tolerance=±5% resistance=10k package=THT]
  C1 = Ceramic Capacitor [capacitance=100nF package="100 mil [THT, multilayer]"]
  C2 = Ceramic Capacitor [capacitance=100nF package="100 mil [THT, multilayer]"]
  R2 = Resistor [tolerance=±5% resistance=220 package=THT]
  R3 = Resistor [tolerance=±5% resistance=220 package=THT]
  R4 = Resistor [tolerance=±5% resistance=220 package=THT]
  R5 = Resistor [tolerance=±5% resistance=220 package=THT]
  SW1 = DIP SWITCH [package=dipswitch-02]
  J2 = male pin header, 7 pins [form="♂ (male)"]
  LED1 = LED - 3mm [color="Red (633nm)" package="3 mm [THT]"]
  J5 = male pin header, 4 pins [form="♂ (male)"]
  J6 = male pin header, 2 pins [form="♂ (male)"]
  J7 = male pin header, 2 pins [form="♂ (male)"]
  C3 = Ceramic Capacitor [capacitance=100nF voltage=6.3V package="200 mil [THT, multilayer]"]
  J4 = shrouded pin header, 6 pins [form="♂ (shrouded male)"]
  S3 = Pushbutton [package=THT]
  J3 = double row female pin header, 8 pins [form="♀ (female)"]
  VCC1 = Battery
  J8 = double row male pin header, 2 pins [form="♂ (male)"]

nets:
  N1: U1.RESET, R1.Pin_1, C3.0, J4.pin3, S3.leg1
  N2: U1.D1_(TX), J2.pin7
  N3: U1.D2, J3.pin5
  N4: U1.D3_(PWM), J2.pin6
  N5: U1.D4, J2.pin5
  3V: U1.VCC, U1.AVCC, R1.Pin_0, C1.1, C2.0, J7.pin1, C3.1, J4.pin6, J3.pin8, J8.pin2
  GND: U1.GND, C1.0, C2.1, SW1.1, SW1.2, J5.pin4, J6.pin2, J7.pin2, J4.pin4, S3.leg0, J3.pin1, VCC1.-
  N6: U1.D5_(PWM), J2.pin4
  N7: U1.D6_(PWM), J2.pin3
  N8: U1.D7, J2.pin2
  N9: U1.D8, J2.pin1
  N10: U1.D9_(PWM), J3.pin2
  N11: U1.D10_(PWM), J3.pin7
  N12: U1.D11_(PWM), J4.pin5, J3.pin6
  N13: U1.D12, J4.pin1, J3.pin4
  N14: U1.D13, J4.pin2, J3.pin3
  N15: U1.A0, R5.Pin_0
  N16: U1.A1, R4.Pin_0
  N17: U1.A2, R3.Pin_0
  N18: U1.A3, R2.Pin_0
  N19: U1.A4, SW1.4
  N20: U1.A5, SW1.3
  N21: R2.Pin_1, LED1.anode
  N22: R3.Pin_1, J5.pin1
  N23: R4.Pin_1, J5.pin2
  N24: R5.Pin_1, J5.pin3
  N25: LED1.cathode, J6.pin1
  N26: VCC1.+, J8.pin1

notes:
  Gnd G R Y
  debug
  C2 R1 C1 R4 C3 R3 R2
  reset
  V+ Gnd
  Device ID
  C3
  C1
  C2
  R1
  R2
  R3
  R4
  R5
  J8
  U1 ATmega328P/PU
  J7
  LED1
  J6
  S3
  SW1
  J5
  J2
  J3
  J4
  MISO
  SCK
  MOSI
  Gnd
  Vcc
  RST
  CE
  CSN
  IRQ
  .
  Modular Alarm System
  Keyboard Module
